// Logisim project Counter2.circ as structural Verilog: 3 circuits, main circuit main
module main (
);

  wire CLK_out, n7447_decoder_1_a_2, n7447_decoder_1_b_2, n7447_decoder_1_c_2, n7447_decoder_1_d_2,
       n7447_decoder_1_e, n7447_decoder_1_f, n7447_decoder_1_g, n7493_decoder_1_a, n7493_decoder_1_b,
       n7493_decoder_1_c, n7493_decoder_1_d;

  Clock CLK (.out(CLK_out));
  _7493_Decoder u_7493_decoder_1 (
    .CLK(CLK_out), .A(n7493_decoder_1_a), .B(n7493_decoder_1_b), .C(n7493_decoder_1_c), .D(n7493_decoder_1_d));
  _7447_Decoder u_7447_decoder_1 (
    .A(n7493_decoder_1_d), .B(n7493_decoder_1_c), .C(n7493_decoder_1_b), .D(n7493_decoder_1_a),
    .a_2(n7447_decoder_1_a_2), .b_2(n7447_decoder_1_b_2), .c_2(n7447_decoder_1_c_2),
    .d_2(n7447_decoder_1_d_2), .e(n7447_decoder_1_e), .f(n7447_decoder_1_f), .g(n7447_decoder_1_g));
  _7_Segment_Display u_7_segment_display_1 (
    .g(n7447_decoder_1_g), .f(n7447_decoder_1_f), .a(n7447_decoder_1_a_2), .b(n7447_decoder_1_b_2),
    .e(n7447_decoder_1_e), .d(n7447_decoder_1_d_2), .c(n7447_decoder_1_c_2));  // open: dp
endmodule

// 7493
module _7493_Decoder (
  input  CLK,
  output A,
  output B,
  output C,
  output D
);

  wire and_1_out, j_k_ff_1_qn, j_k_ff_2_qn, j_k_ff_3_qn;

  J_K_Flip_Flop j_k_ff_1 (
    .J(1'b1), .clk(CLK), .K(1'b1), .Q(A), .Qn(j_k_ff_1_qn), .reset(and_1_out));  // open: preset, en
  J_K_Flip_Flop j_k_ff_2 (
    .J(1'b1), .clk(j_k_ff_1_qn), .K(1'b1), .Q(B), .Qn(j_k_ff_2_qn), .reset(and_1_out));  // open: preset, en
  J_K_Flip_Flop j_k_ff_3 (
    .J(1'b1), .clk(j_k_ff_2_qn), .K(1'b1), .Q(C), .Qn(j_k_ff_3_qn), .reset(and_1_out));  // open: preset, en
  J_K_Flip_Flop j_k_ff_4 (.J(1'b1), .clk(j_k_ff_3_qn), .K(1'b1), .Q(D), .reset(and_1_out));  // open: Qn, preset, en
  and and_1 (and_1_out, B, D);
endmodule

// 7447
module _7447_Decoder (
  input  A,
  input  B,
  input  C,
  input  D,
  output a_2,
  output b_2,
  output c_2,
  output d_2,
  output e,
  output f,
  output g
);

  wire and_1_out, and_2_out, and_3_out, and_4_out, and_5_out, and_6_out, and_7_out, and_8_out, and_9_out,
       and_10_out, and_11_out, and_12_out, and_13_out, and_14_out, and_15_out, and_16_out, and_17_out,
       and_18_out, not_1_out, not_2_out, not_3_out, not_4_out, not_5_out, not_6_out, not_7_out, not_8_out,
       not_9_out, not_10_out, not_11_out, not_12_out, not_13_out, not_14_out, not_15_out, not_16_out,
       not_17_out, not_18_out, not_19_out, not_20_out, not_21_out, not_22_out, or_1_out, or_2_out, or_3_out,
       or_4_out, or_6_out, or_8_out, or_9_out, or_10_out, or_11_out, or_14_out, or_15_out;

  not not_1 (not_1_out, B);
  and and_1 (and_1_out, not_1_out, not_2_out);
  not not_2 (not_2_out, D);
  and and_2 (and_2_out, B, D);
  not not_3 (not_3_out, B);
  not not_4 (not_4_out, C);
  and and_3 (and_3_out, not_4_out, not_5_out);
  not not_5 (not_5_out, D);
  not not_6 (not_6_out, C);
  or or_1 (or_1_out, not_6_out, D);
  not not_7 (not_7_out, B);
  and and_4 (and_4_out, not_7_out, not_8_out);
  not not_8 (not_8_out, D);
  not not_9 (not_9_out, B);
  and and_5 (and_5_out, not_9_out, C);
  not not_10 (not_10_out, D);
  and and_6 (and_6_out, B, not_11_out);
  not not_11 (not_11_out, C);
  not not_12 (not_12_out, B);
  not not_13 (not_13_out, B);
  and and_7 (and_7_out, not_13_out, not_14_out);
  not not_14 (not_14_out, D);
  and and_8 (and_8_out, C, not_15_out);
  not not_15 (not_15_out, D);
  not not_16 (not_16_out, C);
  and and_9 (and_9_out, not_16_out, not_17_out);
  not not_17 (not_17_out, D);
  and and_10 (and_10_out, B, not_18_out);
  not not_18 (not_18_out, C);
  and and_11 (and_11_out, B, not_19_out);
  not not_19 (not_19_out, D);
  not not_20 (not_20_out, B);
  and and_12 (and_12_out, not_20_out, C);
  and and_13 (and_13_out, B, not_21_out);
  not not_21 (not_21_out, C);
  and and_14 (and_14_out, B, not_22_out);
  not not_22 (not_22_out, D);
  or or_2 (or_2_out, and_1_out, C);
  or or_3 (or_3_out, and_2_out, A);
  or or_4 (or_4_out, not_3_out, and_3_out);
  and and_15 (and_15_out, C, D);
  or or_5 (c_2, or_1_out, B);
  or or_6 (or_6_out, and_4_out, and_5_out);
  and and_16 (and_16_out, C, not_10_out);
  and and_17 (and_17_out, and_6_out, D);
  and and_18 (and_18_out, A, not_12_out);
  or or_7 (e, and_7_out, and_8_out);
  or or_8 (or_8_out, and_9_out, and_10_out);
  or or_9 (or_9_out, and_11_out, A);
  or or_10 (or_10_out, and_12_out, and_13_out);
  or or_11 (or_11_out, and_14_out, A);
  or or_12 (a_2, or_2_out, or_3_out);
  or or_13 (b_2, or_4_out, and_15_out);
  or or_14 (or_14_out, or_6_out, and_16_out);
  or or_15 (or_15_out, and_17_out, and_18_out);
  or or_16 (f, or_8_out, or_9_out);
  or or_17 (g, or_10_out, or_11_out);
  or or_18 (d_2, or_14_out, or_15_out);
endmodule
