// Logisim project 152120171029.circ as structural Verilog: 8 circuits, main circuit main
module main (
  input  [3:0] N,
  input  [1:0] S
);

  wire [13:0] a_1_out_2, b_1_out_2, c_1_out_2, multiplexer_1_out;

  A a_1 (.N(N), .out_2(a_1_out_2));
  B b_1 (.N(N), .out_2(b_1_out_2));
  C c_1 (.in_1(N), .out_2(c_1_out_2));
  Multiplexer #(.select(2), .width(14), .enable("false")) multiplexer_1 (
    .in0({14{1'b0}}), .in1(a_1_out_2), .in2(b_1_out_2), .in3(c_1_out_2), .out(multiplexer_1_out), .sel(S));
  _7_Segment_Display u_7_segment_display_1 (
    .g(multiplexer_1_out[7]), .f(multiplexer_1_out[8]), .a(multiplexer_1_out[13]), .b(multiplexer_1_out[12]),
    .e(multiplexer_1_out[9]), .d(multiplexer_1_out[10]), .c(multiplexer_1_out[11]));  // open: dp
  _7_Segment_Display u_7_segment_display_2 (
    .g(multiplexer_1_out[0]), .f(multiplexer_1_out[1]), .a(multiplexer_1_out[6]), .b(multiplexer_1_out[5]),
    .e(multiplexer_1_out[2]), .d(multiplexer_1_out[3]), .c(multiplexer_1_out[4]));  // open: dp

  // Notes on the sheet:
  //   x = 2
  //   01 for a) F = 4N + X
  //   10 for b) F = MOD(N, X)  
  //   11 for c) F = ABS(2N – 3X + 5)  
endmodule

// 7447
module _7447_Decoder (
  input  A,
  input  B,
  input  C,
  input  D,
  output a_2,
  output b_2,
  output c_2,
  output d_2,
  output e,
  output f,
  output g
);

  wire and_1_out, and_2_out, and_3_out, and_4_out, and_5_out, and_6_out, and_7_out, and_8_out, and_9_out,
       and_10_out, and_11_out, and_12_out, and_13_out, and_14_out, and_15_out, and_16_out, and_17_out,
       and_18_out, not_1_out, not_2_out, not_3_out, not_4_out, not_5_out, not_6_out, not_7_out, not_8_out,
       not_9_out, not_10_out, not_11_out, not_12_out, not_13_out, not_14_out, not_15_out, not_16_out,
       not_17_out, not_18_out, not_19_out, not_20_out, not_21_out, not_22_out, or_1_out, or_2_out, or_3_out,
       or_4_out, or_6_out, or_8_out, or_9_out, or_10_out, or_11_out, or_14_out, or_15_out;

  not not_1 (not_1_out, B);
  and and_1 (and_1_out, not_1_out, not_2_out);
  not not_2 (not_2_out, D);
  and and_2 (and_2_out, B, D);
  not not_3 (not_3_out, B);
  not not_4 (not_4_out, C);
  and and_3 (and_3_out, not_4_out, not_5_out);
  not not_5 (not_5_out, D);
  not not_6 (not_6_out, C);
  or or_1 (or_1_out, not_6_out, D);
  not not_7 (not_7_out, B);
  and and_4 (and_4_out, not_7_out, not_8_out);
  not not_8 (not_8_out, D);
  not not_9 (not_9_out, B);
  and and_5 (and_5_out, not_9_out, C);
  not not_10 (not_10_out, D);
  and and_6 (and_6_out, B, not_11_out);
  not not_11 (not_11_out, C);
  not not_12 (not_12_out, B);
  not not_13 (not_13_out, B);
  and and_7 (and_7_out, not_13_out, not_14_out);
  not not_14 (not_14_out, D);
  and and_8 (and_8_out, C, not_15_out);
  not not_15 (not_15_out, D);
  not not_16 (not_16_out, C);
  and and_9 (and_9_out, not_16_out, not_17_out);
  not not_17 (not_17_out, D);
  and and_10 (and_10_out, B, not_18_out);
  not not_18 (not_18_out, C);
  and and_11 (and_11_out, B, not_19_out);
  not not_19 (not_19_out, D);
  not not_20 (not_20_out, B);
  and and_12 (and_12_out, not_20_out, C);
  and and_13 (and_13_out, B, not_21_out);
  not not_21 (not_21_out, C);
  and and_14 (and_14_out, B, not_22_out);
  not not_22 (not_22_out, D);
  or or_2 (or_2_out, and_1_out, C);
  or or_3 (or_3_out, and_2_out, A);
  or or_4 (or_4_out, not_3_out, and_3_out);
  and and_15 (and_15_out, C, D);
  or or_5 (c_2, or_1_out, B);
  or or_6 (or_6_out, and_4_out, and_5_out);
  and and_16 (and_16_out, C, not_10_out);
  and and_17 (and_17_out, and_6_out, D);
  and and_18 (and_18_out, A, not_12_out);
  or or_7 (e, and_7_out, and_8_out);
  or or_8 (or_8_out, and_9_out, and_10_out);
  or or_9 (or_9_out, and_11_out, A);
  or or_10 (or_10_out, and_12_out, and_13_out);
  or or_11 (or_11_out, and_14_out, A);
  or or_12 (a_2, or_2_out, or_3_out);
  or or_13 (b_2, or_4_out, and_15_out);
  or or_14 (or_14_out, or_6_out, and_16_out);
  or or_15 (or_15_out, and_17_out, and_18_out);
  or or_16 (f, or_8_out, or_9_out);
  or or_17 (g, or_10_out, or_11_out);
  or or_18 (d_2, or_14_out, or_15_out);
endmodule

module _4_N_2 (
  input  [3:0] N,
  output out_2,
  output out_3,
  output out_4,
  output out_5,
  output out_6,
  output out_7,
  output out_8,
  output out_9
);

  wire [3:0] multiplier_1_cout, multiplier_1_out;
  wire [7:0] adder_1_out;
  wire [7:4] divider_1_out, divider_1_rem;

  Multiplier #(.width(4)) multiplier_1 (
    .a(N), .b(4'b0100), .out(multiplier_1_out), .cout(multiplier_1_cout));  // open: cin
  Adder adder_1 (.a({multiplier_1_cout, multiplier_1_out}), .b(8'h2), .out(adder_1_out));  // open: cin, cout
  Divider divider_1 (
    .a(adder_1_out), .b(8'ha), .out({divider_1_out, out_2, out_3, out_4, out_5}),
    .rem({divider_1_rem, out_6, out_7, out_8, out_9}));  // open: upper

  // Notes on the sheet:
  //   mod 10
endmodule

module MOD_N_2 (
  input  [3:0] N,
  output out_2,
  output out_3,
  output out_4,
  output out_5
);

  Divider #(.width(4)) divider_1 (.a(N), .b(4'b0010), .rem({out_5, out_4, out_3, out_2}));  // open: out, upper
endmodule

module ABS (
  input  [3:0] N,
  output out_2,
  output out_3,
  output out_4,
  output out_5,
  output out_6,
  output out_7,
  output out_8,
  output out_9,
  output out_10,
  output out_11,
  output out_12,
  output out_13,
  output out_14,
  output out_15,
  output out_16,
  output out_17
);

  wire and_1_out, comparator_1_gt, not_1_out, subtractor_1_bout;
  wire [3:0] multiplier_1_cout, multiplier_1_out;
  wire [7:0] adder_1_out, negator_1_out, subtractor_1_out, transistor_1_out, transistor_2_out;

  Negator negator_1 (.in(transistor_1_out), .out(negator_1_out));
  Transistor #(.\type ("n"), .width(8)) transistor_1 (
    .in(subtractor_1_out), .out(transistor_1_out), .gate(subtractor_1_bout));
  Multiplier #(.width(4)) multiplier_1 (
    .a(N), .b(4'b0010), .out(multiplier_1_out), .cout(multiplier_1_cout));  // open: cin
  and and_1 (and_1_out, subtractor_1_bout, comparator_1_gt);
  Comparator comparator_1 (.a(negator_1_out), .b(8'h5), .gt(comparator_1_gt));  // open: eq, lt
  Subtractor subtractor_1 (
    .a({multiplier_1_cout, multiplier_1_out}), .b(8'h6), .out(subtractor_1_out), .bout(subtractor_1_bout));  // open: bin
  not not_1 (not_1_out, and_1_out);
  Transistor #(.\type ("n"), .width(8)) transistor_2 (.in(adder_1_out), .out(transistor_2_out), .gate(and_1_out));
  Adder adder_1 (.a(subtractor_1_out), .b(8'h5), .out(adder_1_out));  // open: cin, cout
  Transistor #(.\type ("n"), .width(8)) transistor_3 (
    .in(adder_1_out), .out({out_2, out_3, out_4, out_5, out_6, out_7, out_8, out_9}), .gate(not_1_out));
  Negator negator_2 (.in(transistor_2_out), .out({out_10, out_11, out_12, out_13, out_14, out_15, out_16, out_17}));
endmodule

module A (
  input  [3:0] N,
  output [13:0] out_2
);

  wire n4_n_2_1_out_2, n4_n_2_1_out_3, n4_n_2_1_out_4, n4_n_2_1_out_5, n4_n_2_1_out_6, n4_n_2_1_out_7,
       n4_n_2_1_out_8, n4_n_2_1_out_9;

  _4_N_2 u_4_n_2_1 (
    .N(N), .out_2(n4_n_2_1_out_2), .out_3(n4_n_2_1_out_3), .out_4(n4_n_2_1_out_4), .out_5(n4_n_2_1_out_5),
    .out_6(n4_n_2_1_out_6), .out_7(n4_n_2_1_out_7), .out_8(n4_n_2_1_out_8), .out_9(n4_n_2_1_out_9));
  _7447_Decoder u_7447_decoder_1 (
    .A(n4_n_2_1_out_2), .B(n4_n_2_1_out_3), .C(n4_n_2_1_out_4), .D(n4_n_2_1_out_5), .a_2(out_2[13]),
    .b_2(out_2[12]), .c_2(out_2[11]), .d_2(out_2[10]), .e(out_2[9]), .f(out_2[8]), .g(out_2[7]));
  _7447_Decoder u_7447_decoder_2 (
    .A(n4_n_2_1_out_6), .B(n4_n_2_1_out_7), .C(n4_n_2_1_out_8), .D(n4_n_2_1_out_9), .a_2(out_2[6]),
    .b_2(out_2[5]), .c_2(out_2[4]), .d_2(out_2[3]), .e(out_2[2]), .f(out_2[1]), .g(out_2[0]));
endmodule

module B (
  input  [3:0] N,
  output [13:0] out_2
);

  wire MOD_N_2_out_2, MOD_N_2_out_3, MOD_N_2_out_4, MOD_N_2_out_5;

  MOD_N_2 MOD_N_2 (.N(N), .out_2(MOD_N_2_out_2), .out_3(MOD_N_2_out_3), .out_4(MOD_N_2_out_4), .out_5(MOD_N_2_out_5));
  _7447_Decoder u_7447_decoder_1 (
    .A(MOD_N_2_out_5), .B(MOD_N_2_out_4), .C(MOD_N_2_out_3), .D(MOD_N_2_out_2), .a_2(out_2[6]),
    .b_2(out_2[5]), .c_2(out_2[4]), .d_2(out_2[3]), .e(out_2[2]), .f(out_2[1]), .g(out_2[0]));
endmodule

module C (
  input  [3:0] in_1,
  output [13:0] out_2
);

  wire [7:0] abs_1_out_9, divider_1_out, divider_1_rem;

  ABS abs_1 (
    .N(in_1), .out_2(abs_1_out_9[7]), .out_3(abs_1_out_9[6]), .out_4(abs_1_out_9[5]), .out_5(abs_1_out_9[4]),
    .out_6(abs_1_out_9[3]), .out_7(abs_1_out_9[2]), .out_8(abs_1_out_9[1]), .out_9(abs_1_out_9[0]),
    .out_10(abs_1_out_9[7]), .out_11(abs_1_out_9[6]), .out_12(abs_1_out_9[5]), .out_13(abs_1_out_9[4]),
    .out_14(abs_1_out_9[3]), .out_15(abs_1_out_9[2]), .out_16(abs_1_out_9[1]), .out_17(abs_1_out_9[0]));
  Divider divider_1 (.a(abs_1_out_9), .b(8'ha), .out(divider_1_out), .rem(divider_1_rem));  // open: upper
  _7447_Decoder u_7447_decoder_1 (
    .A(divider_1_out[3]), .B(divider_1_out[2]), .C(divider_1_out[1]), .D(divider_1_out[0]), .a_2(out_2[13]),
    .b_2(out_2[12]), .c_2(out_2[11]), .d_2(out_2[10]), .e(out_2[9]), .f(out_2[8]), .g(out_2[7]));
  _7447_Decoder u_7447_decoder_2 (
    .A(divider_1_rem[3]), .B(divider_1_rem[2]), .C(divider_1_rem[1]), .D(divider_1_rem[0]), .a_2(out_2[6]),
    .b_2(out_2[5]), .c_2(out_2[4]), .d_2(out_2[3]), .e(out_2[2]), .f(out_2[1]), .g(out_2[0]));

  // Notes on the sheet:
  //   mod 10
endmodule
